# Fritzing sketch прототип1 (saved by Fritzing 0.9.3b)
breadboards: 1

parts:
  S1 = Pushbutton [package="[THT]"]
  S2 = Pushbutton [package="[THT]"]
  LED1 = LED - 5mm [color="Red (633nm)" package="5 mm [THT]"]
  LED2 = LED - 5mm [color="Green (555nm)" package="5 mm [THT]"]
  Часть2 = Arduino Uno (Rev3)
  VCC1 = Battery  # not connected
  S3 = Toggle Switch [package=THT]
  J1 = Piezo Speaker
  Q1 = NPN-Transistor [package="TO92 [THT]"]
  R1 = Resistor [tolerance=±5% resistance=220 package=THT]
  R2 = Resistor [tolerance=±5% resistance=220 package=THT]

nets:
  N1: S1.Pin_1, S1.Pin_2, S2.Pin_1, S2.Pin_2, S3.L2, R1.Pin_1, R2.Pin_1
  N2: S1.Pin_3, S1.Pin_4, Часть2.D3_PWM
  N3: S2.Pin_3, S2.Pin_4, Часть2.D5_PWM
  N4: LED1.cathode, Часть2.D6_PWM
  N5: LED1.anode, R1.Pin_0
  N6: LED2.cathode, Часть2.D4
  N7: LED2.anode, R2.Pin_0
  N8: Часть2.D2, Q1.B
  N9: J1.pin2, Q1.C
