# Fritzing sketch прототип2 (saved by Fritzing 0.9.3b)
breadboards: 2

parts:
  S1 = Pushbutton [package="[THT]"]
  S2 = Pushbutton [package="[THT]"]
  J1 = Piezo Speaker
  Q1 = NPN-Transistor [package="TO92 [THT]"]
  Disp1 = LBT2088AH [part_number=LBT2088AH]
  Часть1 = TM1637
  YwRobot_Power_Supply1 = YwRobot Breadboard Power Supply [part_number=545043]
  Часть2 = Arduino Nano (Rev3.0)
  Часть3 = Arduino Ethernet Shield (Rev3)  # not connected

nets:
  N1: S1.Pin_1, S1.Pin_2, S2.Pin_1, S2.Pin_2, YwRobot_Power_Supply1.GND#11, YwRobot_Power_Supply1.GND#12
  N2: S1.Pin_3, S1.Pin_4, Часть2.D5
  N3: S2.Pin_3, S2.Pin_4, Часть2.D6
  N4: J1.pin2, Q1.E, Disp1.pin_6, Часть1.GND
  N5: Disp1.pin_7, Часть2.D2
  N6: Disp1.pin_8, Часть1.VCC
  N7: Часть1.DIO, Часть2.D4
  N8: Часть1.CLK, Часть2.D3
  N9: YwRobot_Power_Supply1.VCC#5, YwRobot_Power_Supply1.VCC#6
  N10: YwRobot_Power_Supply1.VCC#9, YwRobot_Power_Supply1.VCC#10
  N11: YwRobot_Power_Supply1.GND#13, YwRobot_Power_Supply1.GND#14

custom parts:
  TM1637: A 4 7-seg display
  YwRobot Breadboard Power Supply: The YwRobot Breadboard Power Supply (MB-V2) has two power rails; they can be 5V or 3V3. Power to the module can be provided through the female USB socket or through the A10 (female) 2.1mm power jack.
